# Fritzing sketch ardufocuser4 (saved by Fritzing 0.9.0b)
perfboards: 2

parts:
  J2 = Generic female header - 4 pins [package=THT]
  M1 = Stepper Motor - Bipolar
  DRV2 = A4983
  C2 = Electrolytic Capacitor [capacitance=0.1mF voltage=16V package="100 mil [THT, electrolytic]"]
  J4 = male pin header, 2 pins [form="♂ (male)"]
  J6 = male pin header, 2 pins [form="♂ (male)"]
  J9 = male pin header, 2 pins [form="♂ (male)"]
  J3 = male pin header, 8 pins [form="♂ (male)"]
  J7 = female pin header, 2 pins [form="♀ (female)"]
  J5 = female pin header, 2 pins [form="♀ (female)"]
  J10 = male pin header, 2 pins [form="♂ (male)"]
  J8 = female pin header, 2 pins [form="♀ (female)"]
  J15 = female pin header, 3 pins [form="♀ (female)"]
  J16 = female pin header, 3 pins [form="♀ (female)"]
  J17 = male pin header, 3 pins [form="♂ (male)"]
  J18 = male pin header, 3 pins [form="♂ (male)"]
  J19 = male pin header, 2 pins [form="♂ (male)"]
  J20 = female pin header, 2 pins [form="♀ (female)"]
  J21 = male pin header, 2 pins [form="♂ (male)"]
  J24 = male pin header, 4 pins [form="♂ (male)"]  # not connected
  J27 = Generic female header - 4 pins [package=THT]
  J28 = male pin header, 1 pin [form="♂ (male)"]
  T1 = LM35 Temperature Sensor [package="TO92 [THT]"]
  J32 = female pin header, 1 pin [form="♀ (female)"]
  J47 = Generic female header - 4 pins [package=THT]
  J48 = male pin header, 2 pins [form="♂ (male)"]  # not connected
  J49 = male pin header, 2 pins [form="♂ (male)"]
  J50 = male pin header, 2 pins [form="♂ (male)"]
  J52 = female pin header, 2 pins [form="♀ (female)"]
  J53 = male pin header, 2 pins [form="♂ (male)"]
  DRV3 = A4983
  J56 = male pin header, 8 pins [form="♂ (male)"]
  J57 = female pin header, 8 pins [form="♀ (female)"]
  J58 = female pin header, 8 pins [form="♀ (female)"]
  J59 = male pin header, 2 pins [form="♂ (male)"]
  J60 = male pin header, 2 pins [form="♂ (male)"]
  J61 = male pin header, 3 pins [form="♂ (male)"]
  J62 = male pin header, 3 pins [form="♂ (male)"]
  J66 = male pin header, 4 pins [form="♂ (male)"]
  J67 = male pin header, 2 pins [form="♂ (male)"]
  J68 = longpad pin header, 3 pins [form="long pad"]
  J69 = male pin header, 2 pins [form="♂ (male)"]
  J70 = male pin header, 2 pins [form="♂ (male)"]
  J71 = male pin header, 3 pins [form="♂ (male)"]
  R28 = Resistor [tolerance=±5% resistance=10k package=THT]  # not connected
  J72 = male pin header, 1 pin [form="♂ (male)"]
  R27 = Resistor [tolerance=±5% resistance=10k package=THT]  # not connected
  R21 = Resistor [tolerance=±5% resistance=10k package=THT]  # not connected
  J30 = male pin header, 3 pins [form="♂ (male)"]
  J31 = male pin header, 1 pin [form="♂ (male)"]
  R20 = Resistor [tolerance=±5% resistance=10k package=THT]
  R5 = Rotary Potentiometer (Small) [maximum_resistance=100kΩ package=THT]
  Arduino1 = Arduino Uno (Rev3)  # not connected
  R6 = Rotary Potentiometer (Small) [maximum_resistance=100kΩ package=THT]
  J29 = female pin header, 3 pins [form="♀ (female)"]
  J51 = female pin header, 2 pins [form="♀ (female)"]
  S5 = Round Pushbutton
  LCD2 = LCD screen
  LCM1602_IIC2 = LCM1602 IIC [part_number="LCM1602 IIC" chip_label="LCM1602 IIC" package="DIP (Dual Inline) [THT]"]
  J65 = longpad pin header, 3 pins [form="long pad"]
  J44 = female pin header, 4 pins [form="♀ (female)"]
  J74 = longpad pin header, 5 pins [form="long pad"]
  LED1 = LED - 5mm [color="Red (633nm)" package="5 mm [THT]"]
  J75 = male pin header, 1 pin [form="♂ (male)"]
  S6 = Round Pushbutton
  J76 = female pin header, 2 pins [form="♀ (female)"]
  J73 = male pin header, 2 pins [form="♂ (male)"]
  J25 = female pin header, 2 pins [form="♀ (female)"]
  J26 = male pin header, 2 pins [form="♂ (male)"]
  J22 = longpad pin header, 2 pins [form="long pad"]
  J45 = longpad pin header, 4 pins [form="long pad"]
  J78 = male pin header, 1 pin [form="♂ (male)"]
  J77 = female pin header, 1 pin [form="♀ (female)"]

nets:
  N1: J2.pin1, M1.D
  N2: J2.pin2, M1.B
  N3: J2.pin3, M1.C
  N4: J2.pin4, M1.A
  N5: DRV2.STEP, J10.pin1
  N6: DRV2.DIR, J10.pin2
  N7: DRV2.VMOT, C2.+, J3.pin1
  N8: DRV2.2B, J3.pin3
  N9: DRV2.2A, J3.pin4
  N10: DRV2.1A, J3.pin5
  N11: DRV2.1B, J3.pin6
  N12: DRV2.VDD, J3.pin7, J17.pin3
  N13: J4.pin1, J5.pin1
  N14: J4.pin2, J5.pin2
  N15: J6.pin1, J7.pin2
  N16: J6.pin2, J7.pin1
  N17: J9.pin1, J8.pin1
  N18: J9.pin2, J8.pin2
  N19: J3.pin2, J30.pin3
  N20: J3.pin8, J17.pin1
  N21: J15.pin1, R5.leg1
  N22: J15.pin2, R5.wiper
  N23: J15.pin3, R5.leg2
  N24: J16.pin1, R6.leg1
  N25: J16.pin2, R6.wiper
  N26: J16.pin3, R6.leg2
  N27: J17.pin2, J19.pin2
  N28: J18.pin2, J19.pin1
  N29: J20.pin1, J21.pin2
  N30: J20.pin2, J21.pin1
  N31: J27.pin1, J47.pin1
  N32: J27.pin2, J47.pin2
  N33: J27.pin3, J47.pin3
  N34: J27.pin4, J47.pin4
  N35: J28.pin1, J32.pin1
  N36: T1.+Vs, J29.pin1
  N37: T1.Vout, J29.pin2
  N38: T1.GND, J29.pin3
  N39: J49.pin2, J50.pin2
  N40: J50.pin1, R20.Pin_0
  N41: J52.pin1, J53.pin1
  N42: J52.pin2, J53.pin2
  N43: DRV3.EN, J58.pin1
  N44: DRV3.MS1, J58.pin2
  N45: DRV3.MS2, J58.pin3
  N46: DRV3.MS3, J58.pin4
  N47: DRV3.RST, J58.pin5
  N48: DRV3.SLP, J58.pin6
  N49: DRV3.STEP, J58.pin7, J59.pin1
  N50: DRV3.DIR, J58.pin8, J59.pin2
  N51: DRV3.VMOT, J57.pin1
  N52: DRV3.GNDMOT, J57.pin2
  N53: DRV3.2B, J56.pin3, J57.pin3
  N54: DRV3.2A, J56.pin4, J57.pin4
  N55: DRV3.1A, J56.pin5, J57.pin5
  N56: DRV3.1B, J56.pin6, J57.pin6
  N57: DRV3.VDD, J57.pin7
  N58: DRV3.GND, J57.pin8
  N59: J56.pin2, J71.pin3
  N60: J56.pin7, J61.pin3
  N61: J56.pin8, J62.pin3
  N62: J60.pin1, J62.pin2
  N63: J60.pin2, J61.pin2
  N64: J66.pin1, J73.pin2
  N65: J67.pin2, J70.pin2
  N66: J68.pin1, J65.pin3, J74.pin3
  N67: J68.pin2, J74.pin4
  N68: J68.pin3, J74.pin5
  N69: J69.pin2, J70.pin1
  N70: J71.pin2, J72.pin1
  N71: J30.pin2, J31.pin1
  N72: J51.pin1, S5.leg0
  N73: J51.pin2, S5.leg1
  VSS: LCD2.VSS, LCM1602_IIC2.VSS
  VDD: LCD2.VDD, LCM1602_IIC2.VDD
  N74: LCD2.V0, LCM1602_IIC2.V0
  N75: LCD2.RS, LCM1602_IIC2.RS
  N76: LCD2.R/W, LCM1602_IIC2.RW
  N77: LCD2.E, LCM1602_IIC2.E
  N78: LCD2.DB0, LCM1602_IIC2.D0
  N79: LCD2.DB1, LCM1602_IIC2.D1
  N80: LCD2.DB2, LCM1602_IIC2.D2
  N81: LCD2.DB3, LCM1602_IIC2.D3
  N82: LCD2.DB4, LCM1602_IIC2.D4
  N83: LCD2.DB5, LCM1602_IIC2.D5
  N84: LCD2.DB6, LCM1602_IIC2.D6
  N85: LCD2.DB7, LCM1602_IIC2.D7
  N86: LCD2.LED+, LCM1602_IIC2.A
  N87: LCD2.LED-, LCM1602_IIC2.K
  N88: LCM1602_IIC2.GND, J44.pin1
  N89: LCM1602_IIC2.VCC, J44.pin2
  N90: LCM1602_IIC2.SDA, J44.pin4
  N91: LCM1602_IIC2.SCL, J44.pin3
  N92: LCM1602_IIC2.LED_A, LCM1602_IIC2.LED_B
  N93: J65.pin2, J74.pin2
  N94: LED1.anode, J78.pin1
  N95: J75.pin1, J77.pin1
  N96: S6.leg0, J76.pin1
  N97: S6.leg1, J76.pin2
  N98: J25.pin1, J26.pin2
  N99: J25.pin2, J26.pin1
  N100: J22.pin1, J45.pin3
  N101: J22.pin2, J45.pin4

notes:
  Nunchaku
  Leyenda:
  Motos:
  STEP_PIN: AZUL-PIN D5
  DIR_PIN: ROSA - PIN D6
  Bumper Sensor:
  BUMP1: BLANCO PIN D3
  BUMP2: NARANJA PIN D2
  Thermal Sensor:
  TSENSR: CIAN PIN A0
  I2C:
  SCL: AMARILLO A5
  SCA: VERDE A4
  POTENCIOMETER:
  POT1: CAFE A2
  POT2: AZUL A1
  LED INDICADOR:
  LED: GRIS PIN 8
  ROJO: 5V
  NEGRO: TIERRA
  Nota 2:
  Las dos resistencias que quedan en el circuito si
  no recuerdo mál son dos resistencias PULL_UP para los bumper
  El sensor LM35 no necesita de resitencias adicionales, solo respetar la polaridad (5v y tierra), terminal centrar a lectura analogica.

custom parts:
  A4983: Poloko A4983 Stepper Motor Control Breakout
  LCM1602 IIC: I2C-Module to use a 1602 or 2004 LCD on with the wire.h libory Serial LCD Modul
