# Fritzing sketch ardufocuser5 (saved by Fritzing 0.9.0b)
perfboards: 2

parts:
  J2 = Generic female header - 4 pins [package=THT]
  M1 = Stepper Motor - Bipolar
  DRV2 = A4983
  C2 = Electrolytic Capacitor [capacitance=0.1mF voltage=16V package="100 mil [THT, electrolytic]"]
  J4 = male pin header, 2 pins [form="♂ (male)"]
  J6 = male pin header, 2 pins [form="♂ (male)"]
  J9 = male pin header, 2 pins [form="♂ (male)"]
  J3 = male pin header, 8 pins [form="♂ (male)"]
  J7 = female pin header, 2 pins [form="♀ (female)"]
  J5 = female pin header, 2 pins [form="♀ (female)"]
  J10 = male pin header, 2 pins [form="♂ (male)"]
  J8 = female pin header, 2 pins [form="♀ (female)"]
  J15 = female pin header, 3 pins [form="♀ (female)"]
  J16 = female pin header, 3 pins [form="♀ (female)"]
  J17 = male pin header, 3 pins [form="♂ (male)"]  # not connected
  J18 = male pin header, 3 pins [form="♂ (male)"]
  J19 = male pin header, 2 pins [form="♂ (male)"]
  J20 = female pin header, 2 pins [form="♀ (female)"]
  J21 = male pin header, 2 pins [form="♂ (male)"]
  J24 = male pin header, 4 pins [form="♂ (male)"]  # not connected
  J27 = Generic female header - 4 pins [package=THT]
  J28 = male pin header, 1 pin [form="♂ (male)"]
  T1 = LM35 Temperature Sensor [package="TO92 [THT]"]
  J32 = female pin header, 1 pin [form="♀ (female)"]
  J47 = Generic female header - 4 pins [package=THT]
  J48 = male pin header, 2 pins [form="♂ (male)"]  # not connected
  J49 = male pin header, 2 pins [form="♂ (male)"]
  J50 = male pin header, 2 pins [form="♂ (male)"]
  J52 = female pin header, 2 pins [form="♀ (female)"]
  J53 = male pin header, 2 pins [form="♂ (male)"]
  R21 = Resistor [tolerance=±5% resistance=10k package=THT]  # not connected
  J30 = male pin header, 3 pins [form="♂ (male)"]
  J31 = male pin header, 1 pin [form="♂ (male)"]
  R20 = Resistor [tolerance=±5% resistance=10k package=THT]
  R5 = Rotary Potentiometer (Small) [maximum_resistance=100kΩ package=THT]
  Arduino1 = Arduino Uno (Rev3)  # not connected
  R6 = Rotary Potentiometer (Small) [maximum_resistance=100kΩ package=THT]
  J29 = female pin header, 3 pins [form="♀ (female)"]
  J51 = female pin header, 2 pins [form="♀ (female)"]
  S5 = Round Pushbutton
  LCD2 = LCD screen
  LCM1602_IIC2 = LCM1602 IIC [part_number="LCM1602 IIC" chip_label="LCM1602 IIC" package="DIP (Dual Inline) [THT]"]
  J44 = female pin header, 4 pins [form="♀ (female)"]
  LED1 = LED - 5mm [color="Red (633nm)" package="5 mm [THT]"]
  J75 = male pin header, 1 pin [form="♂ (male)"]
  S6 = Round Pushbutton
  J76 = female pin header, 2 pins [form="♀ (female)"]
  J25 = female pin header, 2 pins [form="♀ (female)"]
  J26 = male pin header, 2 pins [form="♂ (male)"]
  J22 = longpad pin header, 2 pins [form="long pad"]
  J45 = longpad pin header, 4 pins [form="long pad"]
  J78 = male pin header, 1 pin [form="♂ (male)"]
  J77 = female pin header, 1 pin [form="♀ (female)"]
  LED2 = LED - 5mm [color="Red (633nm)" package="5 mm [THT]"]
  DRV4 = A4983
  C3 = Electrolytic Capacitor [capacitance=0.1mF voltage=16V package="100 mil [THT, electrolytic]"]
  J79 = male pin header, 2 pins [form="♂ (male)"]
  J80 = male pin header, 3 pins [form="♂ (male)"]
  J81 = male pin header, 3 pins [form="♂ (male)"]
  J82 = male pin header, 2 pins [form="♂ (male)"]
  J83 = male pin header, 8 pins [form="♂ (male)"]
  J85 = longpad pin header, 2 pins [form="long pad"]
  J86 = longpad pin header, 4 pins [form="long pad"]
  J87 = male pin header, 4 pins [form="♂ (male)"]  # not connected
  J89 = male pin header, 1 pin [form="♂ (male)"]
  J90 = male pin header, 1 pin [form="♂ (male)"]
  J91 = male pin header, 3 pins [form="♂ (male)"]
  R29 = Resistor [tolerance=±5% resistance=10k package=THT]  # not connected
  R30 = Resistor [tolerance=±5% resistance=10k package=THT]
  J93 = male pin header, 2 pins [form="♂ (male)"]
  J94 = male pin header, 2 pins [form="♂ (male)"]
  J95 = male pin header, 2 pins [form="♂ (male)"]  # not connected
  J96 = male pin header, 3 pins [form="♂ (male)"]

nets:
  N1: J2.pin1, M1.D
  N2: J2.pin2, M1.B
  N3: J2.pin3, M1.C
  N4: J2.pin4, M1.A
  N5: DRV2.MS1, J96.pin1
  N6: DRV2.MS2, J96.pin2
  N7: DRV2.MS3, J96.pin3
  N8: DRV2.STEP, J10.pin1
  N9: DRV2.DIR, J10.pin2
  N10: DRV2.VMOT, C2.+, J3.pin1
  N11: DRV2.2B, J3.pin3
  N12: DRV2.2A, J3.pin4
  N13: DRV2.1A, J3.pin5
  N14: DRV2.1B, J3.pin6
  N15: DRV2.VDD, J3.pin7
  N16: J4.pin1, J5.pin1
  N17: J4.pin2, J5.pin2
  N18: J6.pin1, J7.pin2
  N19: J6.pin2, J7.pin1
  N20: J9.pin1, J8.pin1
  N21: J9.pin2, J8.pin2
  N22: J3.pin2, J30.pin3
  N23: J15.pin1, R5.leg1
  N24: J15.pin2, R5.wiper
  N25: J15.pin3, R5.leg2
  N26: J16.pin1, R6.leg1
  N27: J16.pin2, R6.wiper
  N28: J16.pin3, R6.leg2
  N29: J18.pin2, J19.pin1
  N30: J20.pin1, J21.pin2
  N31: J20.pin2, J21.pin1
  N32: J27.pin1, J47.pin1
  N33: J27.pin2, J47.pin2
  N34: J27.pin3, J47.pin3
  N35: J27.pin4, J47.pin4
  N36: J28.pin1, J32.pin1
  N37: T1.+Vs, J29.pin1
  N38: T1.Vout, J29.pin2
  N39: T1.GND, J29.pin3
  N40: J49.pin2, J50.pin2
  N41: J50.pin1, R20.Pin_0
  N42: J52.pin1, J53.pin1
  N43: J52.pin2, J53.pin2
  N44: J30.pin2, J31.pin1
  N45: J51.pin1, S5.leg0
  N46: J51.pin2, S5.leg1
  VSS: LCD2.VSS, LCM1602_IIC2.VSS
  VDD: LCD2.VDD, LCM1602_IIC2.VDD
  N47: LCD2.V0, LCM1602_IIC2.V0
  N48: LCD2.RS, LCM1602_IIC2.RS
  N49: LCD2.R/W, LCM1602_IIC2.RW
  N50: LCD2.E, LCM1602_IIC2.E
  N51: LCD2.DB0, LCM1602_IIC2.D0
  N52: LCD2.DB1, LCM1602_IIC2.D1
  N53: LCD2.DB2, LCM1602_IIC2.D2
  N54: LCD2.DB3, LCM1602_IIC2.D3
  N55: LCD2.DB4, LCM1602_IIC2.D4
  N56: LCD2.DB5, LCM1602_IIC2.D5
  N57: LCD2.DB6, LCM1602_IIC2.D6
  N58: LCD2.DB7, LCM1602_IIC2.D7
  N59: LCD2.LED+, LCM1602_IIC2.A
  N60: LCD2.LED-, LCM1602_IIC2.K
  N61: LCM1602_IIC2.GND, J44.pin1
  N62: LCM1602_IIC2.VCC, J44.pin2
  N63: LCM1602_IIC2.SDA, J44.pin4
  N64: LCM1602_IIC2.SCL, J44.pin3
  N65: LCM1602_IIC2.LED_A, LCM1602_IIC2.LED_B
  N66: LED1.anode, J78.pin1
  N67: J75.pin1, J77.pin1
  N68: S6.leg0, J76.pin1
  N69: S6.leg1, J76.pin2
  N70: J25.pin1, J26.pin2
  N71: J25.pin2, J26.pin1
  N72: J22.pin1, J45.pin3
  N73: J22.pin2, J45.pin4
  N74: LED2.anode, J89.pin1
  N75: DRV4.STEP, J82.pin1
  N76: DRV4.DIR, J82.pin2
  N77: DRV4.VMOT, C3.+, J83.pin1
  N78: DRV4.2B, J83.pin3
  N79: DRV4.2A, J83.pin4
  N80: DRV4.1A, J83.pin5
  N81: DRV4.1B, J83.pin6
  N82: DRV4.VDD, J81.pin3, J83.pin7
  N83: J79.pin1, J80.pin2
  N84: J79.pin2, J81.pin2
  N85: J81.pin1, J83.pin8
  N86: J83.pin2, J91.pin3
  N87: J85.pin1, J86.pin3
  N88: J85.pin2, J86.pin4
  N89: J90.pin1, J91.pin2
  N90: R30.Pin_0, J93.pin1
  N91: J93.pin2, J94.pin2

notes:
  Nunchaku

custom parts:
  A4983: Poloko A4983 Stepper Motor Control Breakout
  LCM1602 IIC: I2C-Module to use a 1602 or 2004 LCD on with the wire.h libory Serial LCD Modul
