# Fritzing sketch ardufocuser6 (saved by Fritzing 0.9.0b)
perfboards: 3

parts:
  M1 = Stepper Motor - Bipolar
  C2 = Electrolytic Capacitor [capacitance=0.1mF voltage=16V package="100 mil [THT, electrolytic]"]
  J4 = male pin header, 2 pins [form="♂ (male)"]
  J6 = male pin header, 2 pins [form="♂ (male)"]
  J9 = male pin header, 2 pins [form="♂ (male)"]
  J3 = male pin header, 8 pins [form="♂ (male)"]
  J7 = female pin header, 2 pins [form="♀ (female)"]
  J5 = female pin header, 2 pins [form="♀ (female)"]
  J10 = male pin header, 2 pins [form="♂ (male)"]  # not connected
  J8 = female pin header, 2 pins [form="♀ (female)"]
  J15 = female pin header, 3 pins [form="♀ (female)"]
  J16 = female pin header, 3 pins [form="♀ (female)"]
  J17 = male pin header, 3 pins [form="♂ (male)"]  # not connected
  J18 = male pin header, 3 pins [form="♂ (male)"]
  J19 = male pin header, 2 pins [form="♂ (male)"]
  J20 = female pin header, 2 pins [form="♀ (female)"]
  J21 = male pin header, 2 pins [form="♂ (male)"]
  J24 = male pin header, 4 pins [form="♂ (male)"]  # not connected
  J28 = male pin header, 1 pin [form="♂ (male)"]
  J32 = female pin header, 1 pin [form="♀ (female)"]
  J48 = male pin header, 2 pins [form="♂ (male)"]  # not connected
  J49 = male pin header, 2 pins [form="♂ (male)"]
  J50 = male pin header, 2 pins [form="♂ (male)"]
  J52 = female pin header, 2 pins [form="♀ (female)"]
  J53 = male pin header, 2 pins [form="♂ (male)"]
  R21 = Resistor [tolerance=±5% resistance=10k package=THT]  # not connected
  J30 = male pin header, 3 pins [form="♂ (male)"]
  J31 = male pin header, 1 pin [form="♂ (male)"]
  R20 = Resistor [tolerance=±5% resistance=10k package=THT]
  R5 = Rotary Potentiometer (Small) [maximum_resistance=100kΩ package=THT]
  Arduino1 = Arduino Uno (Rev3)  # not connected
  R6 = Rotary Potentiometer (Small) [maximum_resistance=100kΩ package=THT]
  J29 = female pin header, 3 pins [form="♀ (female)"]  # not connected
  J51 = female pin header, 2 pins [form="♀ (female)"]
  S5 = Round Pushbutton
  LCD2 = LCD screen  # not connected
  J44 = female pin header, 4 pins [form="♀ (female)"]  # not connected
  LED1 = LED - 5mm [color="Red (633nm)" package="5 mm [THT]"]
  J75 = male pin header, 1 pin [form="♂ (male)"]
  S6 = Round Pushbutton
  J76 = female pin header, 2 pins [form="♀ (female)"]
  J25 = female pin header, 2 pins [form="♀ (female)"]
  J26 = male pin header, 2 pins [form="♂ (male)"]
  J22 = longpad pin header, 2 pins [form="long pad"]
  J45 = longpad pin header, 4 pins [form="long pad"]
  J78 = male pin header, 1 pin [form="♂ (male)"]
  J77 = female pin header, 1 pin [form="♀ (female)"]
  LED2 = LED - 5mm [color="Red (633nm)" package="5 mm [THT]"]
  C3 = Electrolytic Capacitor [capacitance=0.1mF voltage=16V package="100 mil [THT, electrolytic]"]
  J79 = male pin header, 2 pins [form="♂ (male)"]
  J80 = male pin header, 3 pins [form="♂ (male)"]
  J81 = male pin header, 3 pins [form="♂ (male)"]
  J82 = male pin header, 2 pins [form="♂ (male)"]  # not connected
  J83 = male pin header, 8 pins [form="♂ (male)"]
  J85 = longpad pin header, 2 pins [form="long pad"]
  J86 = longpad pin header, 4 pins [form="long pad"]
  J87 = male pin header, 4 pins [form="♂ (male)"]  # not connected
  J89 = male pin header, 1 pin [form="♂ (male)"]
  J90 = male pin header, 1 pin [form="♂ (male)"]
  J91 = male pin header, 3 pins [form="♂ (male)"]
  R29 = Resistor [tolerance=±5% resistance=10k package=THT]  # not connected
  R30 = Resistor [tolerance=±5% resistance=10k package=THT]
  J93 = male pin header, 2 pins [form="♂ (male)"]
  J94 = male pin header, 2 pins [form="♂ (male)"]
  J95 = male pin header, 2 pins [form="♂ (male)"]  # not connected
  J96 = male pin header, 3 pins [form="♂ (male)"]  # not connected
  J47 = female pin header, 4 pins [form="♀ (female)"]  # not connected
  J2 = female pin header, 4 pins [form="♀ (female)"]
  J27 = female pin header, 4 pins [form="♀ (female)"]  # not connected
  J103 = female pin header, 2 pins [form="♀ (female)"]  # not connected
  J104 = longpad pin header, 2 pins [form="long pad"]  # not connected
  J105 = longpad pin header, 4 pins [form="long pad"]  # not connected
  J106 = male pin header, 4 pins [form="♂ (male)"]  # not connected
  J107 = male pin header, 1 pin [form="♂ (male)"]  # not connected
  J112 = female pin header, 4 pins [form="♀ (female)"]
  LCD3 = LCD screen  # not connected
  Arduino2 = Arduino Uno (Rev3)
  R31 = Rotary Potentiometer (Small) [maximum_resistance=100kΩ package=THT]

nets:
  N1: M1.A, J2.pin4
  N2: M1.C, J2.pin3
  N3: M1.B, J2.pin2
  N4: M1.D, J2.pin1
  N5: C2.+, J3.pin1
  N6: J4.pin1, J5.pin1
  N7: J4.pin2, J5.pin2
  N8: J6.pin1, J7.pin2
  N9: J6.pin2, J7.pin1
  N10: J9.pin1, J8.pin1
  N11: J9.pin2, J8.pin2
  N12: J3.pin2, J30.pin3
  N13: J15.pin1, R5.leg1
  N14: J15.pin2, R5.wiper
  N15: J15.pin3, R5.leg2
  N16: J16.pin1, R6.leg1
  N17: J16.pin2, R6.wiper
  N18: J16.pin3, R6.leg2
  N19: J18.pin2, J19.pin1
  N20: J20.pin1, J21.pin2
  N21: J20.pin2, J21.pin1
  N22: J28.pin1, J32.pin1
  N23: J49.pin2, J50.pin2
  N24: J50.pin1, R20.Pin_0
  N25: J52.pin1, J53.pin1
  N26: J52.pin2, J53.pin2
  N27: J30.pin2, J31.pin1
  N28: J51.pin1, S5.leg0
  N29: J51.pin2, S5.leg1
  N30: LED1.anode, J78.pin1
  N31: J75.pin1, J77.pin1
  N32: S6.leg0, J76.pin1
  N33: S6.leg1, J76.pin2
  N34: J25.pin1, J26.pin2
  N35: J25.pin2, J26.pin1
  N36: J22.pin1, J45.pin3
  N37: J22.pin2, J45.pin4
  N38: LED2.anode, J89.pin1
  N39: C3.+, J83.pin1
  N40: J79.pin1, J80.pin2
  N41: J79.pin2, J81.pin2
  N42: J81.pin1, J83.pin8
  N43: J81.pin3, J83.pin7
  N44: J83.pin2, J91.pin3
  N45: J85.pin1, J86.pin3
  N46: J85.pin2, J86.pin4
  N47: J90.pin1, J91.pin2
  N48: R30.Pin_0, J93.pin1
  N49: J93.pin2, J94.pin2
  N50: J112.pin3, Arduino2.A5/SCL
  N51: Arduino2.A2, R31.wiper
  N52: Arduino2.5V, R31.leg2
  N53: Arduino2.GND, R31.leg1

notes:
  Nunchaku
